# Fritzing sketch tinydrummer (saved by Fritzing 1.0.4)
circuit board: 8.80001cm x 6.50001cm
breadboards: 1

parts:
  10k = Rotary Potentiometer (Small) [maximum_resistance=100kΩ knob_status=50% power=0.5W package=THT]
  10k_2 = Rotary Potentiometer (Small) [maximum_resistance=100kΩ knob_status=50% power=0.5W package=THT]
  10k_3 = Rotary Potentiometer (Small) [maximum_resistance=100kΩ knob_status=50% power=0.5W package=THT]
  Nano = Arduino Nano (Rev3.0)
  VS1053t = female pin header, 5 pins [form="♀ (female)"]
  VS1053b = female pin header, 5 pins [form="♀ (female)"]
  SSD1306 = OLED Mono 0.56 inch blue or white
  LNinGnd = female pin header, 2 pins [form="♀ (female)"]
  M1 = VS1053-mp3-player [package=THT]  # not connected
  RE4 = Rotary Encoder [package=THT]
  220 = Resistor [tolerance=±5% power=0.25W resistance=220 package=THT]
  4_7k = Resistor [tolerance=±5% power=0.25W resistance=4.7k package=THT]
  D4148 = Diode [package=diode-1n4148]
  104 = Ceramic Capacitor [capacitance=100nF voltage=35V package="200 mil [THT, multilayer]"]
  6N138 = IC, DIP package, 8 pins [chip_label=IC]
  J5 = 3.5mm Audio Jack-wq-pj320b.fzpz [package=audio-jack-3.5mm-smd]
  J6 = 3.5mm Audio Jack-wq-pj320b.fzpz [package=audio-jack-3.5mm-smd]

nets:
  ENC_C/GND: 10k.leg1, 10k_2.leg1, 10k_3.leg1, Nano.GND, VS1053t.pin2, SSD1306.GND, RE4.GND, RE4.SW-2, 104.1, 6N138.pin5, J5.pin_4, J6.pin_4
  N1: 10k.wiper, Nano.A0
  5V: 10k.leg2, 10k_2.leg2, 10k_3.leg2, Nano.5V, VS1053t.pin1, SSD1306.VCC, 4_7k.Pin_0, 104.0, 6N138.pin8
  N2: 10k_2.wiper, Nano.A1
  N3: 10k_3.wiper, Nano.A2
  N4: Nano.D0/RX, 4_7k.Pin_1, 6N138.pin6
  ENC_SW: Nano.D2, RE4.SW-1
  ENC_B: Nano.D3, RE4.Pin-A
  ENC_A: Nano.D4, RE4.Pin-B
  DREQ: Nano.D6, VS1053t.pin4
  XDCS: Nano.D7, VS1053b.pin5
  RESET: Nano.D8, VS1053b.pin4
  XCS: Nano.D9, VS1053t.pin5
  MOSI: Nano.D11/MOSI, VS1053t.pin3
  MISO: Nano.D12/MISO, VS1053b.pin2
  SCL: Nano.A5, SSD1306.SCL
  SDA: Nano.A4, SSD1306.SDA
  SCK: Nano.D13/SCK, VS1053b.pin3
  N5: LNinGnd.pin2, J6.pin_2, J6.Pin_3
  N6: 220.Pin_0, D4148.C, 6N138.pin2
  N7: 220.Pin_1, J5.Pin_3
  N8: D4148.A, 6N138.pin3, J5.pin_2

notes:
  VS1053 stacked header representation
  blueprint@poetaster.de 2025
  jlcjlcjlcjlc
  trebuchet v1.0

custom parts:
  OLED Mono 0.56 inch blue or white: OLED, I2C 3.3V - 5V Blue and White text versions
  VS1053-mp3-player: LC Technology VS1003/1053 MP3 Codec module.
  Rotary Encoder: Rotary Encoder with push button
  3.5mm Audio Jack-wq-pj320b.fzpz: 3.5mm Audio Jack WQP-PJ320B is a SMD jack, dia 1/8 inch, female, right angle and through hole.
